// Logisim project Project4.circ as structural Verilog: 14 circuits, main circuit regfile
module CPUmain (
);

  wire alu_1_equal, and_1_out, and_2_out, clock_1_out, clock_2_out, control_1_alu_v_mem_select,
       control_1_beq, control_1_bne, control_1_imm_sel, control_1_j, control_1_jal, control_1_jalr,
       control_1_jr, control_1_reg_write_e, control_1_write_en_mem, not_1_out, or_1_out, or_2_out, or_3_out,
       or_4_out;
  wire [3:0] control_1_alu_code;
  wire [4:0] control_1_rd, control_1_rs, control_1_rt;
  wire [15:0] bit_extender_1_out, bit_extender_2_out;
  wire [31:0] adder_1_out, adder_2_out, alu_1_res, control_1_imm, multiplexer_1_out, multiplexer_2_out,
       multiplexer_3_out, multiplexer_4_out, multiplexer_5_out, multiplexer_6_out, ram_1_dout,
       regfile_1_rs_data, regfile_1_rt_data, register_1_q, rom_1_data, shifter_1_out, shifter_2_out,
       shifter_3_out, shifter_4_out;

  Adder #(.width(32)) adder_1 (.a(register_1_q), .b(32'h4), .out(adder_1_out));  // open: cin, cout
  Shifter #(.width(32)) shifter_1 (.in(control_1_imm), .\dist (5'b00010), .out(shifter_1_out));
  Adder #(.width(32)) adder_2 (.a(adder_1_out), .b(shifter_1_out), .out(adder_2_out));  // open: cin, cout
  Shifter #(.width(32)) shifter_2 (.in(control_1_imm), .\dist (5'b00010), .out(shifter_2_out));
  Multiplexer #(.width(32)) multiplexer_1 (
    .in0(adder_1_out), .in1(adder_2_out), .out(multiplexer_1_out), .sel(or_4_out));
  Multiplexer #(.width(32)) multiplexer_2 (
    .in0(multiplexer_1_out), .in1(multiplexer_3_out), .out(multiplexer_2_out), .sel(or_1_out));
  Multiplexer #(.width(32)) multiplexer_3 (
    .in0(shifter_2_out), .in1(regfile_1_rs_data), .out(multiplexer_3_out), .sel(or_2_out));
  Clock clock_1 (.out(clock_1_out));
  Register #(.width(32)) register_1 (
    .D(multiplexer_2_out), .en(1'b1), .clk(clock_1_out), .Q(register_1_q));  // open: clr
  Shifter #(.shift("lr"), .width(32)) shifter_3 (.in(register_1_q), .\dist (5'b00010), .out(shifter_3_out));
  ROM #(.addrWidth(16), .dataWidth(32)) rom_1 (.addr(bit_extender_1_out), .data(rom_1_data));
  Bit_Extender #(.in_width(32)) bit_extender_1 (.in(shifter_3_out), .out(bit_extender_1_out));
  Multiplexer #(.width(32)) multiplexer_4 (
    .in0(alu_1_res), .in1(ram_1_dout), .out(multiplexer_4_out), .sel(control_1_alu_v_mem_select));
  Multiplexer #(.width(32)) multiplexer_5 (
    .in0(multiplexer_4_out), .in1(adder_1_out), .out(multiplexer_5_out), .sel(or_3_out));
  or or_1 (or_1_out, control_1_jalr, control_1_jr, control_1_jal, control_1_j);
  or or_2 (or_2_out, control_1_jr, control_1_jalr);
  or or_3 (or_3_out, control_1_jal, control_1_jalr);
  Control control_1 (
    .Inst(rom_1_data), .rt(control_1_rt), .rd(control_1_rd), .imm_sel(control_1_imm_sel),
    .ALU_v_MEM_select(control_1_alu_v_mem_select), .write_en_mem(control_1_write_en_mem),
    .ALU_code(control_1_alu_code), .rs(control_1_rs), .imm(control_1_imm),
    .reg_write_e(control_1_reg_write_e), .beq(control_1_beq), .bne(control_1_bne), .j(control_1_j),
    .jal(control_1_jal), .jr(control_1_jr), .jalr(control_1_jalr));  // open: out_6
  regfile regfile_1 (
    .write_e(control_1_reg_write_e), .rd(control_1_rd), .rs(control_1_rs), .rt(control_1_rt),
    .data_in(multiplexer_5_out), .rs_data(regfile_1_rs_data), .rt_data(regfile_1_rt_data));
  or or_4 (or_4_out, and_2_out, and_1_out);
  and and_1 (and_1_out, control_1_bne, not_1_out);
  not not_1 (not_1_out, alu_1_equal);
  Multiplexer #(.width(32)) multiplexer_6 (
    .in0(regfile_1_rt_data), .in1(control_1_imm), .out(multiplexer_6_out), .sel(control_1_imm_sel));
  and and_2 (and_2_out, control_1_beq, alu_1_equal);
  ALU alu_1 (
    .OP2(multiplexer_6_out), .OP1(regfile_1_rs_data), .ALU_CODE(control_1_alu_code), .Res(alu_1_res),
    .equal(alu_1_equal));
  Shifter #(.width(32)) shifter_4 (.in(alu_1_res), .\dist (5'b00010), .out(shifter_4_out));
  RAM #(.addrWidth(16), .dataWidth(32), .enables("line")) ram_1 (
    .addr(bit_extender_2_out), .we(control_1_write_en_mem), .clk(clock_2_out), .din(regfile_1_rt_data),
    .dout(ram_1_dout));
  Bit_Extender #(.in_width(32), .\type ("zero")) bit_extender_2 (.in(shifter_4_out), .out(bit_extender_2_out));
  Clock clock_2 (.out(clock_2_out));

  // Notes on the sheet:
  //   PC + 4 + Offset
  //   branch
  //   jr/jalr
  //   any j
  //   immediate (32 bits, label or offset determined in control)
  //   rs_data
  //   contents of rom_1 (hex, n*v repeats v):
  //   1040000f 23bdfffc afa80000 20080001 1048000f 20080005 1048003d 20080009 10480064 2008000a 10480069
  //   2008000b 10480068 2008000c 1048006a 8000074 23bdf000 201b0000 ac1bf004 8000081 10800022 23bdfffc
  //   afa90000 23bdfffc afaa0000 23bdfffc afab0000 23bdfffc afac0000 3a06020 80402a 200a000a 200b0000
  //   15000011 8a001a 4010 4812 11200004 23bdfffc afa80000 1202020 8000022 21080030 ac08ff00 800002d
  //   13ac000b 8fa80000 21080030 ac08ff00 23bd0004 800002d 42022 200b002d ac0bff00 8000022 20080030
  //   ac08ff00 8fac0000 23bd0004 8fab0000 23bd0004 8faa0000 23bd0004 8fa90000 23bd0004 8fa80000 23bd0004
  //   3400008 23bdfffc afa90000 23bdfffc afaa0000 200a0000 20020000 8c08ff10 15000001 800004a 8c08ff14
  //   2009002d 1128000e 20090030 109482a 15200011 20090039 128482a 1520000e 2108ffd0 2009000a 490018 1012
  //   481020 20080000 ac08ff10 800004a 15400005 14400004 200a0001 20080000 ac08ff10 800004a 11400001 21022
  //   8faa0000 23bd0004 8fa90000 23bd0004 8fa80000 23bd0004 3400008 8c08f004 1001020 884020 ac08f004
  //   8fa80000 23bd0004 3400008 8000074 8fa80000 23bd0004 ac04ff00 3400008 8c08ff10 15000001 8000079
  //   8c02ff14 ac00ff10 8fa80000 23bd0004 3400008 3a08820 a820 2008002a 12a8001b 2008002f 12a80021
  //   2002000c d00c 408020 2008000a 1208006c 402020 c000109 20080028 12080020 2008002a 16080002 2a08020
  //   800009d 2008002b 16080001 800009d 2008002d 16080001 800009d 2008002f 16080081 2a08020 23bdfffc
  //   afb00000 8000083 8fa80000 23bd0004 8fa90000 1280018 4012 afa80000 a820 8000087 8fa80000 23bd0004
  //   8fa90000 128001a 4012 afa80000 a820 8000087 3a09020 20020005 d00c 23bdfffc afa20000 402020 c000106
  //   2002000c d00c 408020 402020 c000109 20080029 1208ffc5 22040000 c00010c 1040006c 10600017 23bdfffc
  //   afb00000 20020005 d00c 23bdfffc afa20000 402020 c000106 80000cb 2002000c d00c 408020 402020 c000109
  //   20080029 12080016 22040000 c00010c 10400058 10600003 23bdfffc afb00000 80000c4 8fa80000 20020005
  //   d00c 405020 402020 c000106 2009002a 12090003 10a001a 4012 80000e6 10a0018 4012 afa80000 80000cb
  //   8fb30000 23bd0004 125d0009 8fa80000 23bd0004 8fa90000 23bd0004 200a002b 11480002 1339822 80000f4
  //   1339820 165dfff6 23bdfffc afb30000 8000083 8fb30000 23bd0004 123d0024 8fa80000 23bd0004 8fa90000
  //   23bd0004 200a002b 11480002 1339822 80000f4 1339820 123d001a 80000fb 20020001 d00c 3e00008 2002000b
  //   d00c 3e00008 200b002a 148b0002 20030000 800011b 200b002b 148b0002 20030001 800011b 200b002d 148b0002
  //   20030001 800011b 200b002f 148b0003 20030000 20020001 3e00008 1020 3e00008 2004003d 2002000b d00c
  //   2602020 20020001 d00c 8000148 2004003d 2002000b d00c 8fa40000 23bd0004 20020001 d00c 2002000b
  //   2004000a d00c 20040049 d00c 2004004e d00c 20040056 d00c 20040041 d00c 2004004c d00c 20040049 d00c
  //   20040044 d00c 20040020 d00c 20040043 d00c 20040048 d00c 20040041 d00c 20040052 d00c 2002000a d00c
  //   ALU/Mem_s
  //   if on, take mem
  //   pc + 4
  //   jal/jalr
  //   jal/jalr
  //   any j
  //   jr/jalr
  //   ALU data
  //   Mem data
  //   successful branch
endmodule

module regfile (
  input  [31:0] data_in,
  input  write_e,
  input  [4:0] rd,
  input  [4:0] rs,
  input  [4:0] rt,
  output [31:0] rs_data,
  output [31:0] rt_data
);

  wire clock_1_out, demultiplexer_1_out1, demultiplexer_1_out2, demultiplexer_1_out3, demultiplexer_1_out4,
       demultiplexer_1_out5, demultiplexer_1_out6, demultiplexer_1_out7, demultiplexer_1_out8,
       demultiplexer_1_out9, demultiplexer_1_out10, demultiplexer_1_out11, demultiplexer_1_out12,
       demultiplexer_1_out13, demultiplexer_1_out14, demultiplexer_1_out15, demultiplexer_1_out16,
       demultiplexer_1_out17, demultiplexer_1_out18, demultiplexer_1_out19, demultiplexer_1_out20,
       demultiplexer_1_out21, demultiplexer_1_out22, demultiplexer_1_out23, demultiplexer_1_out24,
       demultiplexer_1_out25, demultiplexer_1_out26, demultiplexer_1_out27, demultiplexer_1_out28,
       demultiplexer_1_out29, demultiplexer_1_out30, demultiplexer_1_out31;
  wire [31:0] multiplexer_1_out, multiplexer_2_out, multiplexer_3_out, multiplexer_4_out, multiplexer_5_out,
       multiplexer_6_out, multiplexer_7_out, multiplexer_8_out, multiplexer_9_out, multiplexer_10_out,
       multiplexer_11_out, multiplexer_12_out, multiplexer_13_out, multiplexer_14_out, multiplexer_15_out,
       multiplexer_16_out, multiplexer_17_out, multiplexer_18_out, multiplexer_19_out, multiplexer_20_out,
       multiplexer_21_out, multiplexer_22_out, multiplexer_23_out, multiplexer_24_out, multiplexer_25_out,
       multiplexer_26_out, multiplexer_27_out, multiplexer_28_out, multiplexer_29_out, multiplexer_30_out,
       multiplexer_31_out, reg1_q, reg2_q, reg3_q, reg4_q, reg5_q, reg6_q, reg7_q, reg8_q, reg9_q, reg10_q,
       reg11_q, reg12_q, reg13_q, reg14_q, reg15_q, reg16_q, reg17_q, reg18_q, reg19_q, reg20_q, reg21_q,
       reg22_q, reg23_q, reg24_q, reg25_q, reg26_q, reg27_q, reg28_q, reg29_q, reg30_q, reg31_q;

  Demultiplexer #(.select(5)) demultiplexer_1 (
    .out1(demultiplexer_1_out1), .out2(demultiplexer_1_out2), .out3(demultiplexer_1_out3),
    .out4(demultiplexer_1_out4), .out5(demultiplexer_1_out5), .out6(demultiplexer_1_out6),
    .out7(demultiplexer_1_out7), .out8(demultiplexer_1_out8), .out9(demultiplexer_1_out9),
    .out10(demultiplexer_1_out10), .out11(demultiplexer_1_out11), .out12(demultiplexer_1_out12),
    .out13(demultiplexer_1_out13), .out14(demultiplexer_1_out14), .out15(demultiplexer_1_out15),
    .out16(demultiplexer_1_out16), .out17(demultiplexer_1_out17), .out18(demultiplexer_1_out18),
    .out19(demultiplexer_1_out19), .out20(demultiplexer_1_out20), .out21(demultiplexer_1_out21),
    .out22(demultiplexer_1_out22), .out23(demultiplexer_1_out23), .out24(demultiplexer_1_out24),
    .out25(demultiplexer_1_out25), .out26(demultiplexer_1_out26), .out27(demultiplexer_1_out27),
    .out28(demultiplexer_1_out28), .out29(demultiplexer_1_out29), .out30(demultiplexer_1_out30),
    .out31(demultiplexer_1_out31), .in(write_e), .sel(rd));  // open: out0
  Register #(.width(32)) reg1 (.D(multiplexer_1_out), .clk(clock_1_out), .Q(reg1_q));  // open: en, clr
  Multiplexer #(.width(32)) multiplexer_1 (
    .in0(reg1_q), .in1(data_in), .out(multiplexer_1_out), .sel(demultiplexer_1_out1));
  Clock clock_1 (.out(clock_1_out));
  Register #(.width(32)) reg13 (.D(multiplexer_2_out), .clk(clock_1_out), .Q(reg13_q));  // open: en, clr
  Multiplexer #(.width(32)) multiplexer_2 (
    .in0(reg13_q), .in1(data_in), .out(multiplexer_2_out), .sel(demultiplexer_1_out13));
  Register #(.width(32)) reg25 (.D(multiplexer_3_out), .clk(clock_1_out), .Q(reg25_q));  // open: en, clr
  Multiplexer #(.width(32)) multiplexer_3 (
    .in0(reg25_q), .in1(data_in), .out(multiplexer_3_out), .sel(demultiplexer_1_out25));
  Register #(.width(32)) reg2 (.D(multiplexer_4_out), .clk(clock_1_out), .Q(reg2_q));  // open: en, clr
  Multiplexer #(.width(32)) multiplexer_4 (
    .in0(reg2_q), .in1(data_in), .out(multiplexer_4_out), .sel(demultiplexer_1_out2));
  Register #(.width(32)) reg14 (.D(multiplexer_5_out), .clk(clock_1_out), .Q(reg14_q));  // open: en, clr
  Multiplexer #(.width(32)) multiplexer_5 (
    .in0(reg14_q), .in1(data_in), .out(multiplexer_5_out), .sel(demultiplexer_1_out14));
  Register #(.width(32)) reg26 (.D(multiplexer_6_out), .clk(clock_1_out), .Q(reg26_q));  // open: en, clr
  Multiplexer #(.width(32)) multiplexer_6 (
    .in0(reg26_q), .in1(data_in), .out(multiplexer_6_out), .sel(demultiplexer_1_out26));
  Register #(.width(32)) reg3 (.D(multiplexer_7_out), .clk(clock_1_out), .Q(reg3_q));  // open: en, clr
  Multiplexer #(.width(32)) multiplexer_7 (
    .in0(reg3_q), .in1(data_in), .out(multiplexer_7_out), .sel(demultiplexer_1_out3));
  Register #(.width(32)) reg15 (.D(multiplexer_8_out), .clk(clock_1_out), .Q(reg15_q));  // open: en, clr
  Multiplexer #(.width(32)) multiplexer_8 (
    .in0(reg15_q), .in1(data_in), .out(multiplexer_8_out), .sel(demultiplexer_1_out15));
  Register #(.width(32)) reg27 (.D(multiplexer_9_out), .clk(clock_1_out), .Q(reg27_q));  // open: en, clr
  Multiplexer #(.width(32)) multiplexer_9 (
    .in0(reg27_q), .in1(data_in), .out(multiplexer_9_out), .sel(demultiplexer_1_out27));
  Register #(.width(32)) reg4 (.D(multiplexer_10_out), .clk(clock_1_out), .Q(reg4_q));  // open: en, clr
  Multiplexer #(.width(32)) multiplexer_10 (
    .in0(reg4_q), .in1(data_in), .out(multiplexer_10_out), .sel(demultiplexer_1_out4));
  Register #(.width(32)) reg16 (.D(multiplexer_11_out), .clk(clock_1_out), .Q(reg16_q));  // open: en, clr
  Multiplexer #(.width(32)) multiplexer_11 (
    .in0(reg16_q), .in1(data_in), .out(multiplexer_11_out), .sel(demultiplexer_1_out16));
  Register #(.width(32)) reg28 (.D(multiplexer_12_out), .clk(clock_1_out), .Q(reg28_q));  // open: en, clr
  Multiplexer #(.width(32)) multiplexer_12 (
    .in0(reg28_q), .in1(data_in), .out(multiplexer_12_out), .sel(demultiplexer_1_out28));
  Register #(.width(32)) reg5 (.D(multiplexer_13_out), .clk(clock_1_out), .Q(reg5_q));  // open: en, clr
  Multiplexer #(.width(32)) multiplexer_13 (
    .in0(reg5_q), .in1(data_in), .out(multiplexer_13_out), .sel(demultiplexer_1_out5));
  Register #(.width(32)) reg17 (.D(multiplexer_14_out), .clk(clock_1_out), .Q(reg17_q));  // open: en, clr
  Multiplexer #(.width(32)) multiplexer_14 (
    .in0(reg17_q), .in1(data_in), .out(multiplexer_14_out), .sel(demultiplexer_1_out17));
  Register #(.width(32)) reg29 (.D(multiplexer_15_out), .clk(clock_1_out), .Q(reg29_q));  // open: en, clr
  Multiplexer #(.width(32)) multiplexer_15 (
    .in0(reg29_q), .in1(data_in), .out(multiplexer_15_out), .sel(demultiplexer_1_out29));
  Register #(.width(32)) reg6 (.D(multiplexer_16_out), .clk(clock_1_out), .Q(reg6_q));  // open: en, clr
  Multiplexer #(.width(32)) multiplexer_16 (
    .in0(reg6_q), .in1(data_in), .out(multiplexer_16_out), .sel(demultiplexer_1_out6));
  Register #(.width(32)) reg18 (.D(multiplexer_17_out), .clk(clock_1_out), .Q(reg18_q));  // open: en, clr
  Multiplexer #(.width(32)) multiplexer_17 (
    .in0(reg18_q), .in1(data_in), .out(multiplexer_17_out), .sel(demultiplexer_1_out18));
  Register #(.width(32)) reg30 (.D(multiplexer_18_out), .clk(clock_1_out), .Q(reg30_q));  // open: en, clr
  Multiplexer #(.width(32)) multiplexer_18 (
    .in0(reg30_q), .in1(data_in), .out(multiplexer_18_out), .sel(demultiplexer_1_out30));
  Register #(.width(32)) reg7 (.D(multiplexer_19_out), .clk(clock_1_out), .Q(reg7_q));  // open: en, clr
  Multiplexer #(.width(32)) multiplexer_19 (
    .in0(reg7_q), .in1(data_in), .out(multiplexer_19_out), .sel(demultiplexer_1_out7));
  Register #(.width(32)) reg19 (.D(multiplexer_20_out), .clk(clock_1_out), .Q(reg19_q));  // open: en, clr
  Multiplexer #(.width(32)) multiplexer_20 (
    .in0(reg19_q), .in1(data_in), .out(multiplexer_20_out), .sel(demultiplexer_1_out19));
  Register #(.width(32)) reg31 (.D(multiplexer_21_out), .clk(clock_1_out), .Q(reg31_q));  // open: en, clr
  Multiplexer #(.width(32)) multiplexer_21 (
    .in0(reg31_q), .in1(data_in), .out(multiplexer_21_out), .sel(demultiplexer_1_out31));
  Register #(.width(32)) reg8 (.D(multiplexer_22_out), .clk(clock_1_out), .Q(reg8_q));  // open: en, clr
  Multiplexer #(.width(32)) multiplexer_22 (
    .in0(reg8_q), .in1(data_in), .out(multiplexer_22_out), .sel(demultiplexer_1_out8));
  Register #(.width(32)) reg20 (.D(multiplexer_23_out), .clk(clock_1_out), .Q(reg20_q));  // open: en, clr
  Multiplexer #(.width(32)) multiplexer_23 (
    .in0(reg20_q), .in1(data_in), .out(multiplexer_23_out), .sel(demultiplexer_1_out20));
  Register #(.width(32)) reg9 (.D(multiplexer_24_out), .clk(clock_1_out), .Q(reg9_q));  // open: en, clr
  Multiplexer #(.width(32)) multiplexer_24 (
    .in0(reg9_q), .in1(data_in), .out(multiplexer_24_out), .sel(demultiplexer_1_out9));
  Register #(.width(32)) reg21 (.D(multiplexer_25_out), .clk(clock_1_out), .Q(reg21_q));  // open: en, clr
  Multiplexer #(.width(32)) multiplexer_25 (
    .in0(reg21_q), .in1(data_in), .out(multiplexer_25_out), .sel(demultiplexer_1_out21));
  Register #(.width(32)) reg10 (.D(multiplexer_26_out), .clk(clock_1_out), .Q(reg10_q));  // open: en, clr
  Multiplexer #(.width(32)) multiplexer_26 (
    .in0(reg10_q), .in1(data_in), .out(multiplexer_26_out), .sel(demultiplexer_1_out10));
  Register #(.width(32)) reg22 (.D(multiplexer_27_out), .clk(clock_1_out), .Q(reg22_q));  // open: en, clr
  Multiplexer #(.width(32)) multiplexer_27 (
    .in0(reg22_q), .in1(data_in), .out(multiplexer_27_out), .sel(demultiplexer_1_out22));
  Register #(.width(32)) reg11 (.D(multiplexer_28_out), .clk(clock_1_out), .Q(reg11_q));  // open: en, clr
  Multiplexer #(.width(32)) multiplexer_28 (
    .in0(reg11_q), .in1(data_in), .out(multiplexer_28_out), .sel(demultiplexer_1_out11));
  Register #(.width(32)) reg23 (.D(multiplexer_29_out), .clk(clock_1_out), .Q(reg23_q));  // open: en, clr
  Multiplexer #(.width(32)) multiplexer_29 (
    .in0(reg23_q), .in1(data_in), .out(multiplexer_29_out), .sel(demultiplexer_1_out23));
  Register #(.width(32)) reg12 (.D(multiplexer_30_out), .clk(clock_1_out), .Q(reg12_q));  // open: en, clr
  Multiplexer #(.width(32)) multiplexer_30 (
    .in0(reg12_q), .in1(data_in), .out(multiplexer_30_out), .sel(demultiplexer_1_out12));
  Register #(.width(32)) reg24 (.D(multiplexer_31_out), .clk(clock_1_out), .Q(reg24_q));  // open: en, clr
  Multiplexer #(.width(32)) multiplexer_31 (
    .in0(reg24_q), .in1(data_in), .out(multiplexer_31_out), .sel(demultiplexer_1_out24));
  Multiplexer #(.select(5), .width(32)) multiplexer_32 (
    .in0({32{1'b0}}), .in1(reg1_q), .in2(reg2_q), .in3(reg3_q), .in4(reg4_q), .in5(reg5_q), .in6(reg6_q),
    .in7(reg7_q), .in8(reg8_q), .in9(reg9_q), .in10(reg10_q), .in11(reg11_q), .in12(reg12_q), .in13(reg13_q),
    .in14(reg14_q), .in15(reg15_q), .in16(reg16_q), .in17(reg17_q), .in18(reg18_q), .in19(reg19_q),
    .in20(reg20_q), .in21(reg21_q), .in22(reg22_q), .in23(reg23_q), .in24(reg24_q), .in25(reg25_q),
    .in26(reg26_q), .in27(reg27_q), .in28(reg28_q), .in29(reg29_q), .in30(reg30_q), .in31(reg31_q),
    .out(rs_data), .sel(rs));
  Multiplexer #(.select(5), .width(32)) multiplexer_33 (
    .in0({32{1'b0}}), .in1(reg1_q), .in2(reg2_q), .in3(reg3_q), .in4(reg4_q), .in5(reg5_q), .in6(reg6_q),
    .in7(reg7_q), .in8(reg8_q), .in9(reg9_q), .in10(reg10_q), .in11(reg11_q), .in12(reg12_q), .in13(reg13_q),
    .in14(reg14_q), .in15(reg15_q), .in16(reg16_q), .in17(reg17_q), .in18(reg18_q), .in19(reg19_q),
    .in20(reg20_q), .in21(reg21_q), .in22(reg22_q), .in23(reg23_q), .in24(reg24_q), .in25(reg25_q),
    .in26(reg26_q), .in27(reg27_q), .in28(reg28_q), .in29(reg29_q), .in30(reg30_q), .in31(reg31_q),
    .out(rt_data), .sel(rt));
endmodule

module ALU (
  input  [3:0] ALU_CODE,
  input  [31:0] OP1,
  input  [31:0] OP2,
  output [31:0] Res,
  output equal
);

  wire clock_1_out, comparator_2_lt, comparator_3_eq, comparator_4_eq;
  wire [4:0] bit_extender_1_out;
  wire [31:0] adder_1_out, and_1_out, bit_extender_2_out, divider_1_out, divider_1_rem, HI_q, LO_q,
       multiplexer_1_out, multiplexer_2_out, multiplexer_4_out, multiplexer_5_out, multiplier_1_cout,
       multiplier_1_out, nor_1_out, or_1_out, shifter_1_out, shifter_2_out, subtractor_1_out, xor_1_out;

  Bit_Extender #(.in_width(32), .out_width(5)) bit_extender_1 (.in(OP2), .out(bit_extender_1_out));
  Comparator #(.width(32)) comparator_1 (.a(OP1), .b(OP2), .eq(equal));  // open: gt, lt
  assign or_1_out = OP1 | OP2;  // OR_Gate or_1, 32 bits wide
  assign and_1_out = OP1 & OP2;  // AND_Gate and_1, 32 bits wide
  assign xor_1_out = OP1 ^ OP2;  // XOR_Gate xor_1, 32 bits wide
  assign nor_1_out = ~(OP1 | OP2);  // NOR_Gate nor_1, 32 bits wide
  Shifter #(.shift("lr"), .width(32)) shifter_1 (.in(OP1), .\dist (bit_extender_1_out), .out(shifter_1_out));
  Shifter #(.width(32)) shifter_2 (.in(OP1), .\dist (bit_extender_1_out), .out(shifter_2_out));
  Comparator #(.width(32)) comparator_2 (.a(OP1), .b(OP2), .lt(comparator_2_lt));  // open: gt, eq
  Adder #(.width(32)) adder_1 (.a(OP1), .b(OP2), .out(adder_1_out));  // open: cin, cout
  Subtractor #(.width(32)) subtractor_1 (.a(OP1), .b(OP2), .out(subtractor_1_out));  // open: bin, bout
  Multiplier #(.width(32)) multiplier_1 (
    .a(OP1), .b(OP2), .out(multiplier_1_out), .cout(multiplier_1_cout));  // open: cin
  Divider #(.mode("twosComplement"), .width(32)) divider_1 (
    .a(OP1), .b(OP2), .out(divider_1_out), .rem(divider_1_rem));  // open: upper
  assign bit_extender_2_out = {{31{1'b0}}, comparator_2_lt};  // Bit_Extender bit_extender_2
  Multiplexer #(.select(4), .width(32)) multiplexer_1 (
    .in0(adder_1_out), .in1(subtractor_1_out), .in2(multiplier_1_out), .in3(divider_1_out),
    .in6(shifter_2_out), .in7(shifter_1_out), .in8(bit_extender_2_out), .in9(and_1_out), .in10(or_1_out),
    .in11(xor_1_out), .in12(nor_1_out), .out(multiplexer_1_out), .sel(ALU_CODE));  // open: in4, in5, in13, in14, in15
  Comparator #(.width(4)) comparator_3 (.a(ALU_CODE), .b(4'b0100), .eq(comparator_3_eq));  // open: gt, lt
  Comparator #(.width(4)) comparator_4 (.a(ALU_CODE), .b(4'b0101), .eq(comparator_4_eq));  // open: gt, lt
  Multiplexer #(.width(32)) multiplexer_2 (
    .in0(multiplexer_1_out), .in1(LO_q), .out(multiplexer_2_out), .sel(comparator_3_eq));
  Multiplexer #(.width(32)) multiplexer_3 (.in0(multiplexer_2_out), .in1(HI_q), .out(Res), .sel(comparator_4_eq));
  Register #(.width(32)) HI (.D(multiplexer_4_out), .clk(clock_1_out), .Q(HI_q));  // open: en, clr
  Multiplexer #(.select(4), .width(32)) multiplexer_4 (
    .in0(HI_q), .in1(HI_q), .in2(multiplier_1_cout), .in3(divider_1_rem), .in4(HI_q), .in5(HI_q), .in6(HI_q),
    .in7(HI_q), .in8(HI_q), .in9(HI_q), .in10(HI_q), .in11(HI_q), .in12(HI_q), .in13(HI_q), .in14(HI_q),
    .in15(HI_q), .out(multiplexer_4_out), .sel(ALU_CODE));
  Register #(.width(32)) LO (.D(multiplexer_5_out), .clk(clock_1_out), .Q(LO_q));  // open: en, clr
  Multiplexer #(.select(4), .width(32)) multiplexer_5 (
    .in0(LO_q), .in1(LO_q), .in2(multiplier_1_out), .in3(divider_1_out), .in4(LO_q), .in5(LO_q), .in6(LO_q),
    .in7(LO_q), .in8(LO_q), .in9(LO_q), .in10(LO_q), .in11(LO_q), .in12(LO_q), .in13(LO_q), .in14(LO_q),
    .in15(LO_q), .out(multiplexer_5_out), .sel(ALU_CODE));
  Clock clock_1 (.out(clock_1_out));

  // Notes on the sheet:
  //   or
  //   and
  //   shift right
  //   shift left
  //   slt
  //   xor
  //   nor
  //   add
  //   sub
  //   mult
  //   div
endmodule

module Control (
  input  [31:0] Inst,
  output [4:0] rs,
  output [4:0] rt,
  output [4:0] rd,
  output reg_write_e,
  output [5:0] out_6,
  output [31:0] imm,
  output imm_sel,
  output ALU_v_MEM_select,
  output beq,
  output write_en_mem,
  output bne,
  output j,
  output jal,
  output jr,
  output jalr,
  output [3:0] ALU_code
);

  wire and_2_out, and_3_out, and_4_out, and_5_out, and_6_out, and_7_out, and_8_out, comparator_1_eq,
       comparator_2_eq, comparator_8_eq, comparator_9_eq, comparator_10_eq, comparator_11_eq,
       comparator_12_eq, comparator_13_eq, comparator_14_eq, comparator_15_eq, comparator_16_eq,
       comparator_17_eq, comparator_18_eq, comparator_19_eq, comparator_20_eq, comparator_21_eq,
       comparator_22_eq, comparator_23_eq, comparator_24_eq, comparator_25_eq, comparator_26_eq,
       comparator_27_eq, comparator_28_eq, comparator_29_eq, comparator_30_eq, comparator_31_eq,
       comparator_32_eq, comparator_33_eq, comparator_34_eq, comparator_35_eq, comparator_36_eq,
       comparator_37_eq, comparator_38_eq, comparator_39_eq, comparator_40_eq, comparator_41_eq,
       comparator_42_eq, comparator_43_eq, multiplexer_23_out, not_1_out, or_1_out, or_2_out, or_3_out,
       or_6_out, or_7_out, or_10_out, or_11_out;
  wire [3:0] multiplexer_5_out, multiplexer_6_out, multiplexer_7_out, multiplexer_8_out, multiplexer_9_out,
       multiplexer_10_out, multiplexer_11_out, multiplexer_12_out, multiplexer_13_out, multiplexer_14_out,
       multiplexer_15_out, multiplexer_16_out, multiplexer_17_out, multiplexer_18_out, multiplexer_19_out,
       multiplexer_20_out;
  wire [4:0] multiplexer_3_out, multiplexer_4_out, multiplexer_21_out, multiplexer_22_out;
  wire [5:0] multiplexer_1_out;
  wire [15:0] bit_extender_1_out, multiplexer_24_out;
  wire [31:0] bit_extender_2_out, bit_extender_3_out;

  Comparator #(.mode("unsigned"), .width(6)) comparator_1 (
    .a(6'b001000), .b(Inst[31:26]), .eq(comparator_1_eq));  // open: gt, lt
  Comparator #(.mode("unsigned"), .width(6)) comparator_2 (
    .a(6'b100011), .b(Inst[31:26]), .eq(comparator_2_eq));  // open: gt, lt
  Comparator #(.mode("unsigned"), .width(6)) comparator_3 (
    .a(6'b101011), .b(Inst[31:26]), .eq(write_en_mem));  // open: gt, lt
  Comparator #(.mode("unsigned"), .width(6)) comparator_4 (.a(6'b000100), .b(Inst[31:26]), .eq(beq));  // open: gt, lt
  Comparator #(.mode("unsigned"), .width(6)) comparator_5 (.a(6'b000101), .b(Inst[31:26]), .eq(bne));  // open: gt, lt
  Comparator #(.mode("unsigned"), .width(6)) comparator_6 (.a(6'b000010), .b(Inst[31:26]), .eq(j));  // open: gt, lt
  Comparator #(.mode("unsigned"), .width(6)) comparator_7 (.a(6'b000011), .b(Inst[31:26]), .eq(jal));  // open: gt, lt
  Comparator #(.mode("unsigned"), .width(6)) comparator_8 (
    .a({6{1'b0}}), .b(Inst[31:26]), .eq(comparator_8_eq));  // open: gt, lt
  Comparator #(.mode("unsigned"), .width(6)) comparator_9 (
    .a(6'b001000), .b(multiplexer_1_out), .eq(comparator_9_eq));  // open: gt, lt
  Comparator #(.mode("unsigned"), .width(6)) comparator_10 (
    .a(6'b001001), .b(multiplexer_1_out), .eq(comparator_10_eq));  // open: gt, lt
  Comparator #(.mode("unsigned"), .width(6)) comparator_11 (
    .a(6'b001100), .b(multiplexer_1_out), .eq(comparator_11_eq));  // open: gt, lt
  or or_1 (or_1_out, write_en_mem, comparator_1_eq, comparator_2_eq);
  and and_1 (jr, comparator_8_eq, comparator_9_eq);
  Comparator #(.mode("unsigned"), .width(6)) comparator_12 (
    .a(Inst[31:26]), .b(6'b100011), .eq(comparator_12_eq));  // open: gt, lt
  Comparator #(.mode("unsigned"), .width(6)) comparator_13 (
    .a(Inst[31:26]), .b(6'b000011), .eq(comparator_13_eq));  // open: gt, lt
  Comparator #(.mode("unsigned"), .width(6)) comparator_14 (
    .a(Inst[31:26]), .b({6{1'b0}}), .eq(comparator_14_eq));  // open: gt, lt
  or or_2 (or_2_out, comparator_1_eq, comparator_2_eq, write_en_mem);
  or or_3 (or_3_out, j, jal);
  or or_4 (jalr, and_2_out, and_3_out);
  and and_2 (and_2_out, comparator_8_eq, comparator_10_eq);
  and and_3 (and_3_out, comparator_8_eq, comparator_11_eq);
  Comparator #(.mode("unsigned"), .width(6)) comparator_15 (
    .a(Inst[5:0]), .b({6{1'b0}}), .eq(comparator_15_eq));  // open: gt, lt
  Comparator #(.mode("unsigned"), .width(6)) comparator_16 (
    .a(Inst[5:0]), .b(6'b000010), .eq(comparator_16_eq));  // open: gt, lt
  Multiplexer #(.width(6)) multiplexer_1 (.in0(Inst[5:0]), .in1(6'b100000), .out(multiplexer_1_out), .sel(or_1_out));
  or or_5 (ALU_v_MEM_select, comparator_2_eq, beq, bne);
  or or_6 (or_6_out, comparator_15_eq, comparator_16_eq);
  and and_4 (and_4_out, comparator_14_eq, or_6_out);
  and and_5 (and_5_out, comparator_14_eq, comparator_17_eq);
  Comparator #(.mode("unsigned"), .width(6)) comparator_17 (
    .a(Inst[5:0]), .b(6'b001100), .eq(comparator_17_eq));  // open: gt, lt
  Multiplexer #(.width(5)) multiplexer_2 (.in0(Inst[25:21]), .in1(Inst[20:16]), .out(rs), .sel(and_4_out));
  Comparator #(.mode("unsigned"), .width(6)) comparator_18 (
    .a(6'b100000), .b(multiplexer_1_out), .eq(comparator_18_eq));  // open: gt, lt
  Comparator #(.mode("unsigned"), .width(6)) comparator_19 (
    .a(6'b100010), .b(multiplexer_1_out), .eq(comparator_19_eq));  // open: gt, lt
  Comparator #(.mode("unsigned"), .width(6)) comparator_20 (
    .a(6'b011000), .b(multiplexer_1_out), .eq(comparator_20_eq));  // open: gt, lt
  Comparator #(.mode("unsigned"), .width(6)) comparator_21 (
    .a(6'b011010), .b(multiplexer_1_out), .eq(comparator_21_eq));  // open: gt, lt
  Comparator #(.mode("unsigned"), .width(6)) comparator_22 (
    .a(6'b010010), .b(multiplexer_1_out), .eq(comparator_22_eq));  // open: gt, lt
  Comparator #(.mode("unsigned"), .width(6)) comparator_23 (
    .a(6'b010000), .b(multiplexer_1_out), .eq(comparator_23_eq));  // open: gt, lt
  Comparator #(.mode("unsigned"), .width(6)) comparator_24 (
    .a({6{1'b0}}), .b(multiplexer_1_out), .eq(comparator_24_eq));  // open: gt, lt
  Comparator #(.mode("unsigned"), .width(6)) comparator_25 (
    .a(6'b000010), .b(multiplexer_1_out), .eq(comparator_25_eq));  // open: gt, lt
  Comparator #(.mode("unsigned"), .width(6)) comparator_26 (
    .a(6'b101010), .b(multiplexer_1_out), .eq(comparator_26_eq));  // open: gt, lt
  Comparator #(.mode("unsigned"), .width(6)) comparator_27 (
    .a(6'b100100), .b(multiplexer_1_out), .eq(comparator_27_eq));  // open: gt, lt
  Comparator #(.mode("unsigned"), .width(6)) comparator_28 (
    .a(6'b100101), .b(multiplexer_1_out), .eq(comparator_28_eq));  // open: gt, lt
  Comparator #(.mode("unsigned"), .width(6)) comparator_29 (
    .a(6'b100110), .b(multiplexer_1_out), .eq(comparator_29_eq));  // open: gt, lt
  Comparator #(.mode("unsigned"), .width(6)) comparator_30 (
    .a(6'b100111), .b(multiplexer_1_out), .eq(comparator_30_eq));  // open: gt, lt
  Comparator #(.mode("unsigned"), .width(6)) comparator_31 (
    .a(6'b001000), .b(multiplexer_1_out), .eq(comparator_31_eq));  // open: gt, lt
  Comparator #(.mode("unsigned"), .width(6)) comparator_32 (
    .a(6'b001001), .b(multiplexer_1_out), .eq(comparator_32_eq));  // open: gt, lt
  Comparator #(.mode("unsigned"), .width(6)) comparator_33 (
    .a(6'b001100), .b(multiplexer_1_out), .eq(comparator_33_eq));  // open: gt, lt
  Multiplexer #(.width(5)) multiplexer_3 (
    .in0(Inst[15:11]), .in1(Inst[20:16]), .out(multiplexer_3_out), .sel(comparator_1_eq));
  Comparator #(.mode("unsigned"), .width(6)) comparator_34 (
    .a({6{1'b0}}), .b(Inst[5:0]), .eq(comparator_34_eq));  // open: gt, lt
  Comparator #(.mode("unsigned"), .width(6)) comparator_35 (
    .a(6'b000010), .b(Inst[5:0]), .eq(comparator_35_eq));  // open: gt, lt
  Multiplexer #(.width(5)) multiplexer_4 (
    .in0(multiplexer_3_out), .in1({5{1'b1}}), .out(multiplexer_4_out), .sel(comparator_13_eq));
  Multiplexer #(.width(4)) multiplexer_5 (
    .in0(4'b0000), .in1(4'b0000), .out(multiplexer_5_out), .sel(comparator_18_eq));
  Multiplexer #(.width(4)) multiplexer_6 (
    .in0(4'b0000), .in1(4'b0001), .out(multiplexer_6_out), .sel(comparator_19_eq));
  Multiplexer #(.width(4)) multiplexer_7 (
    .in0(4'b0000), .in1(4'b0010), .out(multiplexer_7_out), .sel(comparator_20_eq));
  Multiplexer #(.width(4)) multiplexer_8 (
    .in0(4'b0000), .in1(4'b0011), .out(multiplexer_8_out), .sel(comparator_21_eq));
  Multiplexer #(.width(4)) multiplexer_9 (
    .in0(4'b0000), .in1(4'b0100), .out(multiplexer_9_out), .sel(comparator_22_eq));
  Multiplexer #(.width(4)) multiplexer_10 (
    .in0(4'b0000), .in1(4'b0101), .out(multiplexer_10_out), .sel(comparator_23_eq));
  Multiplexer #(.width(4)) multiplexer_11 (
    .in0(4'b0000), .in1(4'b0110), .out(multiplexer_11_out), .sel(comparator_24_eq));
  Multiplexer #(.width(4)) multiplexer_12 (
    .in0(4'b0000), .in1(4'b0111), .out(multiplexer_12_out), .sel(comparator_25_eq));
  Multiplexer #(.width(4)) multiplexer_13 (
    .in0(4'b0000), .in1(4'b1000), .out(multiplexer_13_out), .sel(comparator_26_eq));
  Multiplexer #(.width(4)) multiplexer_14 (
    .in0(4'b0000), .in1(4'b1001), .out(multiplexer_14_out), .sel(comparator_27_eq));
  Multiplexer #(.width(4)) multiplexer_15 (
    .in0(4'b0000), .in1(4'b1010), .out(multiplexer_15_out), .sel(comparator_28_eq));
  Multiplexer #(.width(4)) multiplexer_16 (
    .in0(4'b0000), .in1(4'b1011), .out(multiplexer_16_out), .sel(comparator_29_eq));
  Multiplexer #(.width(4)) multiplexer_17 (
    .in0(4'b0000), .in1(4'b1100), .out(multiplexer_17_out), .sel(comparator_30_eq));
  Multiplexer #(.width(4)) multiplexer_18 (
    .in0(4'b0000), .in1(4'b0000), .out(multiplexer_18_out), .sel(comparator_31_eq));
  Multiplexer #(.width(4)) multiplexer_19 (
    .in0(4'b0000), .in1(4'b0000), .out(multiplexer_19_out), .sel(comparator_32_eq));
  Multiplexer #(.width(4)) multiplexer_20 (
    .in0(4'b0000), .in1(4'b0000), .out(multiplexer_20_out), .sel(comparator_33_eq));
  Multiplexer #(.width(5)) multiplexer_21 (
    .in0(multiplexer_4_out), .in1(5'b11010), .out(multiplexer_21_out), .sel(and_5_out));
  or or_7 (or_7_out, comparator_34_eq, comparator_35_eq);
  Multiplexer #(.width(5)) multiplexer_22 (
    .in0(multiplexer_21_out), .in1(Inst[20:16]), .out(multiplexer_22_out), .sel(comparator_12_eq));
  Comparator #(.width(5)) comparator_36 (.a(Inst[15:11]), .b({5{1'b0}}), .eq(comparator_36_eq));  // open: gt, lt
  assign bit_extender_1_out = {{11{1'b0}}, Inst[10:6]};  // Bit_Extender bit_extender_1
  and and_6 (and_6_out, multiplexer_23_out, comparator_36_eq);
  Multiplexer multiplexer_23 (.in0(comparator_40_eq), .in1(1'b0), .out(multiplexer_23_out), .sel(comparator_1_eq));
  Multiplexer #(.width(16)) multiplexer_24 (
    .in0(Inst[15:0]), .in1(bit_extender_1_out), .out(multiplexer_24_out), .sel(and_7_out));
  and and_7 (and_7_out, comparator_14_eq, or_7_out);
  Multiplexer #(.width(5)) multiplexer_25 (.in0(multiplexer_22_out), .in1({5{1'b1}}), .out(rd), .sel(and_6_out));
  Comparator #(.mode("unsigned"), .width(6)) comparator_37 (
    .a(Inst[5:0]), .b(6'b011000), .eq(comparator_37_eq));  // open: gt, lt
  Comparator #(.mode("unsigned"), .width(6)) comparator_38 (
    .a(Inst[5:0]), .b(6'b011010), .eq(comparator_38_eq));  // open: gt, lt
  Comparator #(.mode("unsigned"), .width(6)) comparator_39 (
    .a(Inst[5:0]), .b(6'b001000), .eq(comparator_39_eq));  // open: gt, lt
  Comparator #(.mode("unsigned"), .width(6)) comparator_40 (
    .a(Inst[5:0]), .b(6'b001001), .eq(comparator_40_eq));  // open: gt, lt
  assign bit_extender_2_out = {{16{multiplexer_24_out[15]}}, multiplexer_24_out};  // Bit_Extender bit_extender_2
  or or_8 (imm_sel, and_7_out, or_2_out);
  assign ALU_code = multiplexer_5_out | multiplexer_6_out | multiplexer_7_out | multiplexer_8_out | multiplexer_9_out | multiplexer_10_out | multiplexer_11_out | multiplexer_12_out | multiplexer_13_out | multiplexer_14_out | multiplexer_15_out | multiplexer_16_out | multiplexer_17_out | multiplexer_18_out | multiplexer_19_out | multiplexer_20_out;  // OR_Gate or_9, 4 bits wide
  or or_10 (or_10_out, comparator_37_eq, comparator_38_eq, comparator_39_eq);
  assign bit_extender_3_out = {{6{1'b0}}, Inst[25:0]};  // Bit_Extender bit_extender_3
  and and_8 (and_8_out, comparator_14_eq, or_10_out);
  Comparator #(.mode("unsigned"), .width(6)) comparator_41 (
    .a(Inst[31:26]), .b(6'b100011), .eq(comparator_41_eq));  // open: gt, lt
  Comparator #(.mode("unsigned"), .width(6)) comparator_42 (
    .a(Inst[31:26]), .b(6'b001000), .eq(comparator_42_eq));  // open: gt, lt
  Comparator #(.mode("unsigned"), .width(6)) comparator_43 (
    .a(Inst[31:26]), .b(6'b000011), .eq(comparator_43_eq));  // open: gt, lt
  not not_1 (not_1_out, and_8_out);
  or or_11 (or_11_out, comparator_41_eq, comparator_42_eq, comparator_43_eq);
  Multiplexer multiplexer_26 (.in0(or_11_out), .in1(not_1_out), .out(reg_write_e), .sel(comparator_14_eq));
  Multiplexer #(.width(32)) multiplexer_27 (
    .in0(bit_extender_2_out), .in1(bit_extender_3_out), .out(imm), .sel(or_3_out));

  assign out_6 = Inst[5:0];
  assign rt = Inst[20:16];

  // Notes on the sheet:
  //   op
  //   addi
  //   lw
  //   sw
  //   beq
  //   bne
  //   j
  //   jr/jalr/sys
  //   jal
  //   jalr
  //   opcode
  //   rs/target
  //   rt/rd/target
  //   rd/imm/target
  //   shamt/imm
  //   func/imm
  //   jr
  //   syscall (like jalr)
  //   ALU=0
  //   imm_s_on
  //   lw
  //   jal
  //   lw, beq, bne
  //   j or jal
  //   sll
  //   slr
  //   addi
  //   just sw
  //   func
  //   syscall
  //   add
  //   sub
  //   mult
  //   div
  //   mflo
  //   mfhi
  //   sll
  //   srl
  //   slt
  //   and
  //   or
  //   xor
  //   nor
  //   jr
  //   jalr
  //   syscall
  //   sll
  //   srl
  //   check if opcode = 0, otherwise last 5 could be an int that matches func of other instruction
  //   sets to $ra if no
  //   register specified
  //   func
  //   mult
  //   div
  //   jr
  //   jalr
  //   op code
  //   target
  //   lw
  //   addi
  //   jal
endmodule

module MemoryController (
  input  WriteEnableFromBus,
  input  [25:0] AddressFromBus,
  input  [31:0] DataFromBus,
  input  [31:0] DataFromMem,
  output [31:0] DataToBus,
  output WriteToBus,
  output WriteEnableToMem,
  output [23:0] AddressToMem,
  output [31:0] DataToMem
);

  wire comparator_1_lt, not_1_out;
  wire [25:0] shifter_1_out;

  Comparator #(.mode("unsigned"), .width(26)) comparator_1 (
    .a(AddressFromBus), .b(26'h3ffff00), .lt(comparator_1_lt));  // open: gt, eq
  not not_1 (not_1_out, WriteEnableFromBus);
  and and_1 (WriteEnableToMem, WriteEnableFromBus, comparator_1_lt);
  Shifter #(.shift("lr"), .width(26)) shifter_1 (.in(AddressFromBus), .\dist (5'b00010), .out(shifter_1_out));
  Bit_Extender #(.in_width(26), .out_width(24), .\type ("zero")) bit_extender_1 (
    .in(shifter_1_out), .out(AddressToMem));
  and and_2 (WriteToBus, not_1_out, comparator_1_lt);
  assign DataToMem = WriteEnableToMem ? DataFromBus : 32'bz;  // Controlled_Buffer controlled_buffer_1
  assign DataToBus = WriteToBus ? DataFromMem : 32'bz;  // Controlled_Buffer controlled_buffer_2
endmodule

module KeyboardController (
  input  [31:0] DataFromBus,
  input  WriteEnableFromBus,
  input  [25:0] AddressFromBus,
  input  [6:0] KeyboardData,
  input  KeyboardStatus,
  output WriteToBus,
  output [31:0] DataToBus,
  output KeyboardRead
);

  wire and_2_out, and_3_out, comparator_1_eq, comparator_2_eq, not_1_out;
  wire [31:0] bit_extender_1_out, bit_extender_2_out, controlled_buffer_1_out, controlled_buffer_2_out;

  not not_1 (not_1_out, WriteEnableFromBus);
  Comparator #(.width(26)) comparator_1 (.a(AddressFromBus), .b(26'h3ffff10), .eq(comparator_1_eq));  // open: gt, lt
  and and_1 (KeyboardRead, WriteEnableFromBus, comparator_1_eq);
  Comparator #(.width(26)) comparator_2 (.a(AddressFromBus), .b(26'h3ffff14), .eq(comparator_2_eq));  // open: gt, lt
  assign bit_extender_1_out = {{25{1'b0}}, KeyboardData};  // Bit_Extender bit_extender_1
  and and_2 (and_2_out, not_1_out, comparator_1_eq);
  and and_3 (and_3_out, not_1_out, comparator_2_eq);
  assign controlled_buffer_1_out = and_3_out ? bit_extender_1_out : 32'bz;  // Controlled_Buffer controlled_buffer_1
  assign bit_extender_2_out = {{31{1'b0}}, KeyboardStatus};  // Bit_Extender bit_extender_2
  assign controlled_buffer_2_out = and_2_out ? bit_extender_2_out : 32'bz;  // Controlled_Buffer controlled_buffer_2
  or or_1 (WriteToBus, and_2_out, and_3_out);
  Multiplexer #(.width(32)) multiplexer_1 (
    .in0(controlled_buffer_1_out), .in1(controlled_buffer_2_out), .out(DataToBus), .sel(and_2_out));

  // Notes on the sheet:
  //   does this even get used?
endmodule

module Computer (
);

  wire clock_1_out, clock_2_out, clock_3_out, cpu_1_buswriteenable,
       hexdigitdisplaycontroller_1_writeenabledtohexdigit, keyboard_1_avail,
       keyboardcontroller_1_keyboardread, keyboardcontroller_1_writetobus,
       ledbarcontroller_1_writeenabledtoledbar, ledmatrixcontroller_1_writeenabledfromledmatrixcontroller,
       memorycontroller_1_writeenabletomem, memorycontroller_1_writetobus, rgb_video_1_p8, rgb_video_1_p9,
       terminalcontroller_1_writetoterminal;
  wire [3:0] controlled_buffer_5_out, controlled_buffer_6_out, controlled_buffer_7_out,
       controlled_buffer_8_out, controlled_buffer_9_out, controlled_buffer_10_out, controlled_buffer_11_out,
       controlled_buffer_12_out, hexdigitdisplaycontroller_1_digit1, hexdigitdisplaycontroller_1_digit2,
       hexdigitdisplaycontroller_1_digit3, hexdigitdisplaycontroller_1_digit4, ledmatrixcontroller_1_column1,
       ledmatrixcontroller_1_column2, ledmatrixcontroller_1_column3, ledmatrixcontroller_1_column4;
  wire [6:0] keyboard_1_data, terminalcontroller_1_datatoterminal;
  wire [7:0] controlled_buffer_4_out, ledbarcontroller_1_datatoledbar, rgb_video_1_p10, rgb_video_1_p11;
  wire [23:0] memorycontroller_1_addresstomem, rgb_video_1_p12;
  wire [25:0] cpu_1_addresstobus;
  wire [31:0] controlled_buffer_1_out, cpu_1_datatobus, keyboardcontroller_1_datatobus,
       memorycontroller_1_datatobus, memorycontroller_1_datatomem, ram_1_dout;

  RAM #(.addrWidth(24), .dataWidth(32), .enables("line")) ram_1 (
    .addr(memorycontroller_1_addresstomem), .we(memorycontroller_1_writeenabletomem), .clk(clock_1_out),
    .din(memorycontroller_1_datatomem), .dout(ram_1_dout));
  Clock clock_1 (.out(clock_1_out));
  Clock clock_2 (.out(clock_2_out));
  Keyboard keyboard_1 (
    .clk(clock_2_out), .re(keyboardcontroller_1_keyboardread), .avail(keyboard_1_avail),
    .data(keyboard_1_data));  // open: clr
  LedBar ledbar_1 (
    .led0(controlled_buffer_4_out[0]), .led1(controlled_buffer_4_out[1]), .led2(controlled_buffer_4_out[2]),
    .led3(controlled_buffer_4_out[3]), .led4(controlled_buffer_4_out[4]), .led5(controlled_buffer_4_out[5]),
    .led6(controlled_buffer_4_out[6]), .led7(controlled_buffer_4_out[7]));
  MemoryController memorycontroller_1 (
    .WriteEnableFromBus(cpu_1_buswriteenable), .AddressFromBus(cpu_1_addresstobus), .DataFromMem(ram_1_dout),
    .DataFromBus(controlled_buffer_1_out), .WriteEnableToMem(memorycontroller_1_writeenabletomem),
    .DataToBus(memorycontroller_1_datatobus), .AddressToMem(memorycontroller_1_addresstomem),
    .DataToMem(memorycontroller_1_datatomem), .WriteToBus(memorycontroller_1_writetobus));
  CPU cpu_1 (
    .DataFromBus(controlled_buffer_1_out), .AddressToBus(cpu_1_addresstobus),
    .BusWriteEnable(cpu_1_buswriteenable), .DataToBus(cpu_1_datatobus));
  assign controlled_buffer_1_out = memorycontroller_1_writetobus ? memorycontroller_1_datatobus : 32'bz;  // Controlled_Buffer controlled_buffer_1
  assign controlled_buffer_1_out = cpu_1_buswriteenable ? cpu_1_datatobus : 32'bz;  // Controlled_Buffer controlled_buffer_2
  assign controlled_buffer_1_out = keyboardcontroller_1_writetobus ? keyboardcontroller_1_datatobus : 32'bz;  // Controlled_Buffer controlled_buffer_3
  KeyboardController keyboardcontroller_1 (
    .DataFromBus(controlled_buffer_1_out), .WriteEnableFromBus(cpu_1_buswriteenable),
    .AddressFromBus(cpu_1_addresstobus), .KeyboardData(keyboard_1_data), .KeyboardStatus(keyboard_1_avail),
    .WriteToBus(keyboardcontroller_1_writetobus), .DataToBus(keyboardcontroller_1_datatobus),
    .KeyboardRead(keyboardcontroller_1_keyboardread));
  assign controlled_buffer_4_out = ledbarcontroller_1_writeenabledtoledbar ? ledbarcontroller_1_datatoledbar : 8'bz;  // Controlled_Buffer controlled_buffer_4
  LEDBarController ledbarcontroller_1 (
    .WriteEnabledFromBus(cpu_1_buswriteenable), .AddressFromBus(cpu_1_addresstobus),
    .DataFromBus(controlled_buffer_1_out), .WriteEnabledToLEDBar(ledbarcontroller_1_writeenabledtoledbar),
    .DataToLEDBar(ledbarcontroller_1_datatoledbar));
  TTY tty_1 (
    .data(terminalcontroller_1_datatoterminal), .clk(clock_3_out), .we(terminalcontroller_1_writetoterminal));  // open: clr
  Clock clock_3 (.out(clock_3_out));
  // RGB_Video #(.height(256), .scale(1), .width(256)) rgb_video_1: pin names not known; wires that end beside it: controlled_buffer_4_out[1], controlled_buffer_4_out[2], controlled_buffer_4_out[3], controlled_buffer_4_out[4], controlled_buffer_4_out[5], controlled_buffer_4_out[6], controlled_buffer_4_out[7], rgb_video_1_p8, rgb_video_1_p9, rgb_video_1_p10, rgb_video_1_p11, rgb_video_1_p12
  Clock clock_4 (.out(rgb_video_1_p8));
  TerminalController terminalcontroller_1 (
    .WriteEnableFromBus(cpu_1_buswriteenable), .AddressFromBus(cpu_1_addresstobus),
    .DataFromBus(controlled_buffer_1_out), .WriteToTerminal(terminalcontroller_1_writetoterminal),
    .DataToTerminal(terminalcontroller_1_datatoterminal));
  RGBController rgbcontroller_1 (
    .AddressFromBus(cpu_1_addresstobus), .DataFromBus(controlled_buffer_1_out),
    .WriteEnable(cpu_1_buswriteenable), .RGBX(rgb_video_1_p10), .RGBY(rgb_video_1_p11),
    .RGBColor(rgb_video_1_p12), .RGBWrite(rgb_video_1_p9));
  HexDigitDisplayController hexdigitdisplaycontroller_1 (
    .WriteEnabledToHexDigit(hexdigitdisplaycontroller_1_writeenabledtohexdigit),
    .Digit1(hexdigitdisplaycontroller_1_digit1), .Digit2(hexdigitdisplaycontroller_1_digit2),
    .Digit3(hexdigitdisplaycontroller_1_digit3), .Digit4(hexdigitdisplaycontroller_1_digit4));  // open: WriteEnabledFromBus, AddressFromBus, DataFromBus
  assign controlled_buffer_5_out = hexdigitdisplaycontroller_1_writeenabledtohexdigit ? hexdigitdisplaycontroller_1_digit1 : 4'bz;  // Controlled_Buffer controlled_buffer_5
  LEDMatrixController ledmatrixcontroller_1 (
    .WriteEnabledFromBus(cpu_1_buswriteenable), .AddressFromBus(cpu_1_addresstobus),
    .DataFromBus(controlled_buffer_1_out),
    .WriteEnabledFromLEDMatrixController(ledmatrixcontroller_1_writeenabledfromledmatrixcontroller),
    .Column1(ledmatrixcontroller_1_column1), .Column2(ledmatrixcontroller_1_column2),
    .Column3(ledmatrixcontroller_1_column3), .Column4(ledmatrixcontroller_1_column4));
  assign controlled_buffer_6_out = ledmatrixcontroller_1_writeenabledfromledmatrixcontroller ? ledmatrixcontroller_1_column1 : 4'bz;  // Controlled_Buffer controlled_buffer_6
  assign controlled_buffer_7_out = hexdigitdisplaycontroller_1_writeenabledtohexdigit ? hexdigitdisplaycontroller_1_digit2 : 4'bz;  // Controlled_Buffer controlled_buffer_7
  assign controlled_buffer_8_out = hexdigitdisplaycontroller_1_writeenabledtohexdigit ? hexdigitdisplaycontroller_1_digit3 : 4'bz;  // Controlled_Buffer controlled_buffer_8
  assign controlled_buffer_9_out = hexdigitdisplaycontroller_1_writeenabledtohexdigit ? hexdigitdisplaycontroller_1_digit4 : 4'bz;  // Controlled_Buffer controlled_buffer_9
  assign controlled_buffer_10_out = ledmatrixcontroller_1_writeenabledfromledmatrixcontroller ? ledmatrixcontroller_1_column2 : 4'bz;  // Controlled_Buffer controlled_buffer_10
  assign controlled_buffer_11_out = ledmatrixcontroller_1_writeenabledfromledmatrixcontroller ? ledmatrixcontroller_1_column3 : 4'bz;  // Controlled_Buffer controlled_buffer_11
  assign controlled_buffer_12_out = ledmatrixcontroller_1_writeenabledfromledmatrixcontroller ? ledmatrixcontroller_1_column4 : 4'bz;  // Controlled_Buffer controlled_buffer_12
  Hex_Digit_Display hex_digit_display_1 (.value(controlled_buffer_9_out));  // open: dp
  Hex_Digit_Display hex_digit_display_2 (.value(controlled_buffer_8_out));  // open: dp
  DotMatrix #(.matrixcols(4), .matrixrows(4)) dotmatrix_1 (
    .col0(controlled_buffer_6_out), .col1(controlled_buffer_10_out), .col2(controlled_buffer_11_out),
    .col3(controlled_buffer_12_out));
  Hex_Digit_Display hex_digit_display_3 (.value(controlled_buffer_7_out));  // open: dp
  Hex_Digit_Display hex_digit_display_4 (.value(controlled_buffer_5_out));  // open: dp

  // Notes on the sheet:
  //   starts after IO and OS
  //   initialize $sp to 0x3FFF000
  //   addi $sp, $0, -4096
  //   we only want one circuit to write to bus at a time
  //   stack pointer should no longer start at zero, initialize it to where it supposed to start
  //   Never want multiple circuits to write to the data wire at the same time, prevent this by using BusWriteEnable
  //   Write_enable
  //   Address
  //   Data
endmodule

module CPU (
  input  [31:0] DataFromBus,
  output [25:0] AddressToBus,
  output BusWriteEnable,
  output [31:0] DataToBus
);

  wire alu_1_equal, and_1_out, and_2_out, clock_1_out, control_1_alu_v_mem_select, control_1_beq,
       control_1_bne, control_1_imm_sel, control_1_j, control_1_jal, control_1_jalr, control_1_jr,
       control_1_reg_write_e, not_1_out, or_1_out, or_2_out, or_3_out, or_4_out;
  wire [3:0] control_1_alu_code;
  wire [4:0] control_1_rd, control_1_rs, control_1_rt;
  wire [15:0] bit_extender_1_out;
  wire [31:0] adder_1_out, adder_2_out, alu_1_res, control_1_imm, multiplexer_1_out, multiplexer_2_out,
       multiplexer_3_out, multiplexer_4_out, multiplexer_5_out, multiplexer_6_out, regfile_1_rs_data,
       register_1_q, rom_1_data, shifter_1_out, shifter_2_out, shifter_3_out;

  Adder #(.width(32)) adder_1 (.a(register_1_q), .b(32'h4), .out(adder_1_out));  // open: cin, cout
  Shifter #(.width(32)) shifter_1 (.in(control_1_imm), .\dist (5'b00010), .out(shifter_1_out));
  Adder #(.width(32)) adder_2 (.a(adder_1_out), .b(shifter_1_out), .out(adder_2_out));  // open: cin, cout
  Shifter #(.width(32)) shifter_2 (.in(control_1_imm), .\dist (5'b00010), .out(shifter_2_out));
  Multiplexer #(.width(32)) multiplexer_1 (
    .in0(adder_1_out), .in1(adder_2_out), .out(multiplexer_1_out), .sel(or_4_out));
  Multiplexer #(.width(32)) multiplexer_2 (
    .in0(multiplexer_1_out), .in1(multiplexer_3_out), .out(multiplexer_2_out), .sel(or_1_out));
  Multiplexer #(.width(32)) multiplexer_3 (
    .in0(shifter_2_out), .in1(regfile_1_rs_data), .out(multiplexer_3_out), .sel(or_2_out));
  Clock clock_1 (.out(clock_1_out));
  Register #(.width(32)) register_1 (
    .D(multiplexer_2_out), .en(1'b1), .clk(clock_1_out), .Q(register_1_q));  // open: clr
  Shifter #(.shift("lr"), .width(32)) shifter_3 (.in(register_1_q), .\dist (5'b00010), .out(shifter_3_out));
  ROM #(.addrWidth(16), .dataWidth(32)) rom_1 (.addr(bit_extender_1_out), .data(rom_1_data));
  Bit_Extender #(.in_width(32)) bit_extender_1 (.in(shifter_3_out), .out(bit_extender_1_out));
  Multiplexer #(.width(32)) multiplexer_4 (
    .in0(alu_1_res), .in1(DataFromBus), .out(multiplexer_4_out), .sel(control_1_alu_v_mem_select));
  Multiplexer #(.width(32)) multiplexer_5 (
    .in0(multiplexer_4_out), .in1(adder_1_out), .out(multiplexer_5_out), .sel(or_3_out));
  or or_1 (or_1_out, control_1_jalr, control_1_jr, control_1_jal, control_1_j);
  or or_2 (or_2_out, control_1_jr, control_1_jalr);
  or or_3 (or_3_out, control_1_jal, control_1_jalr);
  Control control_1 (
    .Inst(rom_1_data), .rt(control_1_rt), .rd(control_1_rd), .imm_sel(control_1_imm_sel),
    .ALU_v_MEM_select(control_1_alu_v_mem_select), .write_en_mem(BusWriteEnable),
    .ALU_code(control_1_alu_code), .rs(control_1_rs), .imm(control_1_imm),
    .reg_write_e(control_1_reg_write_e), .beq(control_1_beq), .bne(control_1_bne), .j(control_1_j),
    .jal(control_1_jal), .jr(control_1_jr), .jalr(control_1_jalr));  // open: out_6
  regfile regfile_1 (
    .write_e(control_1_reg_write_e), .rd(control_1_rd), .rs(control_1_rs), .rt(control_1_rt),
    .data_in(multiplexer_5_out), .rs_data(regfile_1_rs_data), .rt_data(DataToBus));
  or or_4 (or_4_out, and_2_out, and_1_out);
  and and_1 (and_1_out, control_1_bne, not_1_out);
  not not_1 (not_1_out, alu_1_equal);
  Multiplexer #(.width(32)) multiplexer_6 (
    .in0(DataToBus), .in1(control_1_imm), .out(multiplexer_6_out), .sel(control_1_imm_sel));
  and and_2 (and_2_out, control_1_beq, alu_1_equal);
  ALU alu_1 (
    .OP2(multiplexer_6_out), .OP1(regfile_1_rs_data), .ALU_CODE(control_1_alu_code), .Res(alu_1_res),
    .equal(alu_1_equal));
  Bit_Extender #(.in_width(32), .out_width(26), .\type ("zero")) bit_extender_2 (.in(alu_1_res), .out(AddressToBus));

  // Notes on the sheet:
  //   PC + 4 + Offset
  //   branch
  //   jr/jalr
  //   any j
  //   immediate (32 bits, label or offset determined in control)
  //   rs_data
  //   contents of rom_1 (hex, n*v repeats v):
  //   1040000f 23bdfffc afa80000 20080001 1048000f 20080005 1048003d 20080009 10480064 2008000a 10480069
  //   2008000b 10480068 2008000c 1048006a 8000074 23bdf000 201b0000 ac1bf004 8000081 10800022 23bdfffc
  //   afa90000 23bdfffc afaa0000 23bdfffc afab0000 23bdfffc afac0000 3a06020 80402a 200a000a 200b0000
  //   15000011 8a001a 4010 4812 11200004 23bdfffc afa80000 1202020 8000022 21080030 ac08ff00 800002d
  //   13ac000b 8fa80000 21080030 ac08ff00 23bd0004 800002d 42022 200b002d ac0bff00 8000022 20080030
  //   ac08ff00 8fac0000 23bd0004 8fab0000 23bd0004 8faa0000 23bd0004 8fa90000 23bd0004 8fa80000 23bd0004
  //   3400008 23bdfffc afa90000 23bdfffc afaa0000 200a0000 20020000 8c08ff10 15000001 800004a 8c08ff14
  //   2009002d 1128000e 20090030 109482a 15200011 20090039 128482a 1520000e 2108ffd0 2009000a 490018 1012
  //   481020 20080000 ac08ff10 800004a 15400005 14400004 200a0001 20080000 ac08ff10 800004a 11400001 21022
  //   8faa0000 23bd0004 8fa90000 23bd0004 8fa80000 23bd0004 3400008 8c08f004 1001020 884020 ac08f004
  //   8fa80000 23bd0004 3400008 8000074 8fa80000 23bd0004 ac04ff00 3400008 8c08ff10 15000001 8000079
  //   8c02ff14 ac00ff10 8fa80000 23bd0004 3400008 3a08820 a020 a820 b020 2008002a 12a8002b 2008002f
  //   12a80035 2008002d 1288001b 2002000c d00c 408020 2008000a 12080095 2002020 c000136 20080028 12080036
  //   2008002a 16080002 200a820 8000085 2008002b 16080001 80000a3 2008002d 16080002 200a020 8000085
  //   2008002f 160800b2 200a820 8000085 23bdfffc afb00000 8000085 22d60001 20080002 16c8ffe2 8fa80000
  //   2009002b afa90000 84022 23bdfffc afa80000 a020 b020 800008b 22d60001 20080002 16c8ffd6 8fa80000
  //   23bd0004 8fa90000 1280018 4012 afa80000 a820 b020 800008b 22d60001 20080002 16c8ffca 8fa80000
  //   23bd0004 8fa90000 128001a 4012 afa80000 a820 b020 800008b 3a09020 20020005 d00c 23bdfffc afa20000
  //   402020 c000133 2002000c d00c 408020 402020 c000136 20080029 1208ffad 22040000 c000139 10400078
  //   1060002a 200b002b 160b001a 23bdfffc afb00000 80000e1 20020005 d00c 23bdfffc afa20000 402020 c000133
  //   80000e8 2002000c d00c 408020 402020 c000136 20080029 12080026 22040000 c000139 10400061 10600013
  //   200b002b 160b0003 23bdfffc afb00000 80000e1 200b002d 160b0059 80000fb 20020005 d00c 25022 402020
  //   c000133 2008002b 23bdfffc afa80000 23bdfffc afaa0000 80000e8 8fa80000 20020005 d00c 405020 402020
  //   c000133 2009002a 12090003 10a001a 4012 8000113 10a0018 4012 afa80000 80000e8 8fb30000 23bd0004
  //   125d0009 8fa80000 23bd0004 8fa90000 23bd0004 200a002b 11480002 1339822 8000121 1339820 165dfff6
  //   23bdfffc afb30000 8000085 8fb30000 23bd0004 123d0024 8fa80000 23bd0004 8fa90000 23bd0004 200a002b
  //   11480002 1339822 8000131 1339820 123d001a 8000128 20020001 d00c 3e00008 2002000b d00c 3e00008
  //   200b002a 148b0002 20030000 8000148 200b002b 148b0002 20030001 8000148 200b002d 148b0002 20030001
  //   8000148 200b002f 148b0003 20030000 20020001 3e00008 1020 3e00008 2004003d 2002000b d00c 2602020
  //   20020001 d00c 800016e 2002000b 2004000a d00c 20040049 d00c 2004004e d00c 20040056 d00c 20040041 d00c
  //   2004004c d00c 20040049 d00c 20040044 d00c 20040020 d00c 20040043 d00c 20040048 d00c 20040041 d00c
  //   20040052 d00c 2002000a d00c
  //   ALU/Mem_s
  //   if on, take mem
  //   pc + 4
  //   jal/jalr
  //   jal/jalr
  //   any j
  //   jr/jalr
  //   ALU data
  //   Mem data
  //   successful branch
endmodule

module RGBController (
  input  [25:0] AddressFromBus,
  input  [31:0] DataFromBus,
  input  WriteEnable,
  output [7:0] RGBX,
  output [7:0] RGBY,
  output [23:0] RGBColor,
  output RGBWrite
);

  wire and_1_out, and_2_out, and_3_out, and_4_out, clock_1_out, comparator_1_eq, comparator_2_eq,
       comparator_3_eq, comparator_4_eq;
  wire [7:0] bit_extender_1_out, bit_extender_2_out;
  wire [23:0] bit_extender_3_out;

  Comparator #(.width(26)) comparator_1 (.a(AddressFromBus), .b(26'h3ffff20), .eq(comparator_1_eq));  // open: gt, lt
  Comparator #(.width(26)) comparator_2 (.a(AddressFromBus), .b(26'h3ffff24), .eq(comparator_2_eq));  // open: gt, lt
  Comparator #(.width(26)) comparator_3 (.a(AddressFromBus), .b(26'h3ffff28), .eq(comparator_3_eq));  // open: gt, lt
  Comparator #(.width(26)) comparator_4 (.a(AddressFromBus), .b(26'h3ffff2c), .eq(comparator_4_eq));  // open: gt, lt
  and and_1 (and_1_out, WriteEnable, comparator_1_eq);
  and and_2 (and_2_out, WriteEnable, comparator_2_eq);
  and and_3 (and_3_out, WriteEnable, comparator_3_eq);
  and and_4 (and_4_out, comparator_4_eq, WriteEnable);
  Register Xcoord (.D(bit_extender_1_out), .en(and_1_out), .clk(clock_1_out), .Q(RGBX));  // open: clr
  Bit_Extender #(.in_width(32), .out_width(8)) bit_extender_1 (.in(DataFromBus), .out(bit_extender_1_out));
  Register Ycoord (.D(bit_extender_2_out), .en(and_2_out), .clk(clock_1_out), .Q(RGBY));  // open: clr
  Bit_Extender #(.in_width(32), .out_width(8)) bit_extender_2 (.in(DataFromBus), .out(bit_extender_2_out));
  Register #(.width(24)) Color (.D(bit_extender_3_out), .en(and_3_out), .clk(clock_1_out), .Q(RGBColor));  // open: clr
  Bit_Extender #(.in_width(32), .out_width(24)) bit_extender_3 (.in(DataFromBus), .out(bit_extender_3_out));
  Clock clock_1 (.out(clock_1_out));
  assign RGBWrite = and_4_out ? and_4_out : 1'bz;  // Controlled_Buffer controlled_buffer_1
endmodule

module TerminalController (
  input  WriteEnableFromBus,
  input  [25:0] AddressFromBus,
  input  [31:0] DataFromBus,
  output WriteToTerminal,
  output [6:0] DataToTerminal
);

  wire comparator_1_eq;

  Comparator #(.width(26)) comparator_1 (.a(AddressFromBus), .b(26'h3ffff00), .eq(comparator_1_eq));  // open: gt, lt
  Bit_Extender #(.in_width(32), .out_width(7), .\type ("zero")) bit_extender_1 (.in(DataFromBus), .out(DataToTerminal));
  and and_1 (WriteToTerminal, WriteEnableFromBus, comparator_1_eq);
endmodule

module LEDMatrixNumberController (
  input  WriteEnabledFromBus,
  input  [25:0] AddressFromBus,
  input  [31:0] DataFromBus,
  output WriteEnabledFromLEDMatrixController,
  output [5:0] Column1,
  output [5:0] Column2,
  output [5:0] Column3
);

  wire comparator_1_eq;
  wire [3:0] bit_extender_1_out;

  Comparator #(.width(26)) comparator_1 (.a(AddressFromBus), .b(26'h3ffff30), .eq(comparator_1_eq));  // open: gt, lt
  Bit_Extender #(.in_width(32), .out_width(4)) bit_extender_1 (.in(DataFromBus), .out(bit_extender_1_out));
  and and_1 (WriteEnabledFromLEDMatrixController, WriteEnabledFromBus, comparator_1_eq);
  Multiplexer #(.select(4), .width(6)) multiplexer_1 (
    .in0({6{1'b1}}), .in1(6'b010001), .in2(6'b010011), .in3(6'b010001), .in4(6'b111000), .in5(6'b011101),
    .in6(6'b011111), .in7(6'b100000), .in8(6'b011111), .in9(6'b111000), .out(Column1),
    .sel(bit_extender_1_out));  // open: in10, in11, in12, in13, in14, in15
  Multiplexer #(.select(4), .width(6)) multiplexer_2 (
    .in0(6'b100001), .in1({6{1'b1}}), .in2(6'b100101), .in3(6'b010101), .in4(6'b001000), .in5(6'b010101),
    .in6(6'b010101), .in7(6'b100000), .in8(6'b010101), .in9(6'b101000), .out(Column2),
    .sel(bit_extender_1_out));  // open: in10, in11, in12, in13, in14, in15
  Multiplexer #(.select(4), .width(6)) multiplexer_3 (
    .in0({6{1'b1}}), .in1(6'b000001), .in2(6'b011001), .in3(6'b011111), .in4({6{1'b1}}), .in5(6'b010111),
    .in6(6'b010111), .in7({6{1'b1}}), .in8(6'b011111), .in9({6{1'b1}}), .out(Column3),
    .sel(bit_extender_1_out));  // open: in10, in11, in12, in13, in14, in15
endmodule

module LEDBarController (
  input  WriteEnabledFromBus,
  input  [25:0] AddressFromBus,
  input  [31:0] DataFromBus,
  output WriteEnabledToLEDBar,
  output [7:0] DataToLEDBar
);

  wire comparator_1_eq;

  Comparator #(.width(26)) comparator_1 (.a(AddressFromBus), .b(26'h3ffff34), .eq(comparator_1_eq));  // open: gt, lt
  Bit_Extender #(.in_width(32), .out_width(8)) bit_extender_1 (.in(DataFromBus), .out(DataToLEDBar));
  and and_1 (WriteEnabledToLEDBar, WriteEnabledFromBus, comparator_1_eq);
  LedBar ledbar_1 (
    .led0(DataToLEDBar[0]), .led1(DataToLEDBar[1]), .led2(DataToLEDBar[2]), .led3(DataToLEDBar[3]),
    .led4(DataToLEDBar[4]), .led5(DataToLEDBar[5]), .led6(DataToLEDBar[6]), .led7(DataToLEDBar[7]));
endmodule

module LEDMatrixController (
  input  WriteEnabledFromBus,
  input  [25:0] AddressFromBus,
  input  [31:0] DataFromBus,
  output WriteEnabledFromLEDMatrixController,
  output [3:0] Column1,
  output [3:0] Column2,
  output [3:0] Column3,
  output [3:0] Column4
);

  wire comparator_1_eq;

  Comparator #(.width(26)) comparator_1 (.a(AddressFromBus), .b(26'h3ffff38), .eq(comparator_1_eq));  // open: gt, lt
  Bit_Extender #(.in_width(32)) bit_extender_1 (.in(DataFromBus), .out({Column4, Column3, Column2, Column1}));
  and and_1 (WriteEnabledFromLEDMatrixController, WriteEnabledFromBus, comparator_1_eq);
endmodule

module HexDigitDisplayController (
  input  WriteEnabledFromBus,
  input  [25:0] AddressFromBus,
  input  [31:0] DataFromBus,
  output WriteEnabledToHexDigit,
  output [3:0] Digit1,
  output [3:0] Digit2,
  output [3:0] Digit3,
  output [3:0] Digit4
);

  wire comparator_1_eq;

  Comparator #(.width(26)) comparator_1 (.a(AddressFromBus), .b(26'h3ffff30), .eq(comparator_1_eq));  // open: gt, lt
  Bit_Extender #(.in_width(32)) bit_extender_1 (.in(DataFromBus), .out({Digit4, Digit3, Digit2, Digit1}));
  and and_1 (WriteEnabledToHexDigit, WriteEnabledFromBus, comparator_1_eq);
endmodule
